# Fritzing sketch WeatherStation (saved by Fritzing 0.9.3b)
breadboards: 1

parts:
  LED1 = LED - 5mm [color="Red (633nm)" package="5 mm [THT]"]
  LED2 = LED - 5mm [color="Green (570nm)" package="5 mm [THT]"]
  R1 = Resistor [tolerance=±5% resistance=220 package="1206 [SMD]"]
  R2 = Resistor [tolerance=±5% resistance=220 package="1206 [SMD]"]
  Componente2 = Barometric Pressure Sensor - BMP180 Breakout (GY-68)  # not connected
  Componente3 = Arduino Nano (Rev3.0)
  Componente4 = Real Time Clock Module - DS1307 RTC Breakout Board  # not connected
  DHT1 = DHT11 Humitidy and Temperature Sensor  # not connected

nets:
  N1: LED1.cathode, R1.Pin_1
  N2: LED1.anode, Componente3.D4
  N3: LED2.cathode, R2.Pin_1
  N4: LED2.anode, Componente3.D3
  N5: R1.Pin_0, R2.Pin_0

custom parts:
  DHT11 Humitidy and Temperature Sensor: DHT11 Humidity and Temperature Sensor
